# Fritzing sketch main (saved by Fritzing 0.9.5d)
breadboards: 1

parts:
  U1 = NodeMCU V3.0
  HC-SR04_Sensor_1 = HC-SR04 Ultrasonic Distance Sensor
  HC-SR04_Sensor_2 = HC-SR04 Ultrasonic Distance Sensor
  HC-SR04_Sensor_3 = HC-SR04 Ultrasonic Distance Sensor
  M2 = LJ18A3-H-ZBX [package=THT]
  M3 = LJ18A3-H-ZBX [package=THT]
  M4 = LJ18A3-H-ZBX [package=THT]
  J1 = Basic Servo
  J2 = Basic Servo
  HC-SR04_Sensor_4 = HC-SR04 Ultrasonic Distance Sensor

nets:
  N1: U1.D0, J2.pulse
  N2: U1.D1, J1.pulse
  N3: U1.D2, M2.VO_(BLU)
  N4: U1.D3, M3.VO_(BLU)
  N5: U1.D4, M4.VO_(BLU)
  VCC: U1.3V3, M2.VI_(BRN), M3.VI_(BRN), M4.VI_(BRN), J1.vcc, J2.vcc, HC-SR04_Sensor_4.VCC
  GND: U1.GND, HC-SR04_Sensor_1.GND, HC-SR04_Sensor_2.GND, HC-SR04_Sensor_3.GND, M2.SIG_(BLK), M3.SIG_(BLK), M4.SIG_(BLK), J1.gnd, J2.gnd, HC-SR04_Sensor_4.GND
  N6: U1.D5, HC-SR04_Sensor_3.TRIG
  N7: U1.D6, HC-SR04_Sensor_3.ECHO
  N8: U1.D7, HC-SR04_Sensor_2.TRIG
  N9: U1.D8, HC-SR04_Sensor_2.ECHO
  N10: U1.RX, HC-SR04_Sensor_1.TRIG
  N11: U1.TX, HC-SR04_Sensor_1.ECHO
  VCC_2: U1.Vin, HC-SR04_Sensor_1.VCC, HC-SR04_Sensor_2.VCC, HC-SR04_Sensor_3.VCC
  N12: U1.SD2, HC-SR04_Sensor_4.ECHO
  N13: U1.SD3, HC-SR04_Sensor_4.TRIG

custom parts:
  NodeMCU V3.0: NodeMcu V3 Lua WIFI Development Board
  LJ18A3-H-ZBX: LJ18A3-H-ZBX Proximity Sensor module.
