# Fritzing sketch mini (saved by Fritzing 0.9.5d)
breadboards: 1

parts:
  U1 = NodeMCU V3.0
  HC-SR04_Sensor_1 = HC-SR04 Ultrasonic Distance Sensor

nets:
  N1: U1.D0, HC-SR04_Sensor_1.ECHO
  N2: U1.D1, HC-SR04_Sensor_1.TRIG
  3V3: U1.3V3, HC-SR04_Sensor_1.VCC
  GND: U1.GND, HC-SR04_Sensor_1.GND

custom parts:
  NodeMCU V3.0: NodeMcu V3 Lua WIFI Development Board
