# Fritzing sketch prototype (saved by Fritzing 0.9.5d)
breadboards: 1

parts:
  U1 = NodeMCU V3.0
  HC-SR04_Sensor_1 = HC-SR04 Ultrasonic Distance Sensor
  HC-SR04_Sensor_2 = HC-SR04 Ultrasonic Distance Sensor
  J1 = Basic Servo
  M1 = LJ18A3-H-ZBX [package=THT]
  J2 = Basic Servo

nets:
  N1: U1.D0, HC-SR04_Sensor_2.TRIG
  N2: U1.D1, HC-SR04_Sensor_2.ECHO
  N3: U1.D2, HC-SR04_Sensor_1.TRIG
  N4: U1.D3, HC-SR04_Sensor_1.ECHO
  N5: U1.D4, M1.SIG_(BLK)
  VCC: U1.3V3, HC-SR04_Sensor_1.VCC, J1.vcc
  GND: U1.GND, HC-SR04_Sensor_1.GND, J1.gnd
  N6: U1.SD2, J2.pulse
  N7: U1.SD3, J1.pulse

custom parts:
  NodeMCU V3.0: NodeMcu V3 Lua WIFI Development Board
  LJ18A3-H-ZBX: LJ18A3-H-ZBX Proximity Sensor module.
